// Logisim project Relatorio1.circ as structural Verilog
module Meio_Subtrator (
  input  A,
  input  B,
  output S,
  output Tout
);

  xor xor_1 (S, A, B);
  and and_1 (Tout, B, ~A);  // AND_Gate
endmodule

module Subtrator_Completo (
  input  A,
  input  B,
  input  Bin,
  output Sub,
  output Bout
);

  wire meio_subtrator_1_s, meio_subtrator_1_tout, meio_subtrator_2_tout;

  Meio_Subtrator meio_subtrator_1 (.A(A), .B(B), .S(meio_subtrator_1_s), .Tout(meio_subtrator_1_tout));
  Meio_Subtrator meio_subtrator_2 (.A(meio_subtrator_1_s), .B(Bin), .S(Sub), .Tout(meio_subtrator_2_tout));
  or or_1 (Bout, meio_subtrator_2_tout, meio_subtrator_1_tout);
endmodule

module Meio_Somador (
  input  A,
  input  B,
  output Sum,
  output Cout
);

  xor xor_1 (Sum, A, B);
  and and_1 (Cout, A, B);
endmodule

module Somador_Completo (
  input  A,
  input  B,
  input  Cin,
  output Sum,
  output Cout
);

  wire meio_somador_1_cout, meio_somador_1_sum, meio_somador_2_cout;

  Meio_Somador meio_somador_1 (.A(A), .B(B), .Sum(meio_somador_1_sum), .Cout(meio_somador_1_cout));
  Meio_Somador meio_somador_2 (.A(meio_somador_1_sum), .B(Cin), .Sum(Sum), .Cout(meio_somador_2_cout));
  or or_1 (Cout, meio_somador_2_cout, meio_somador_1_cout);
endmodule

module Meio_Sub_Meio_Som_Mux (
  input  [1:0] A_B,
  input  [1:0] A_B_2,
  input  in_3,
  output [1:0] S_Cout
);

  wire [1:0] meio_somador_sum, meio_subtrator_tout;

  Meio_Subtrator meio_subtrator (.A(A_B[1]), .B(A_B[0]), .S(meio_subtrator_tout[1]), .Tout(meio_subtrator_tout[0]));
  Meio_Somador meio_somador (.A(A_B_2[0]), .B(A_B_2[1]), .Sum(meio_somador_sum[0]), .Cout(meio_somador_sum[1]));
  Multiplexer #(.width(2), .enable("false")) multiplexer_1 (
    .in0(meio_subtrator_tout), .in1(meio_somador_sum), .out(S_Cout), .sel(in_3));
endmodule

module Subtrator_Somador_Mux (
  input  [2:0] A_B,
  input  [2:0] A_B_2,
  input  in_3,
  output [1:0] S_Cout
);

  wire [1:0] somador_completo_sum, subtrator_completo_bout;

  Subtrator_Completo subtrator_completo (
    .A(A_B[2]), .B(A_B[1]), .Bin(A_B[0]), .Sub(subtrator_completo_bout[1]), .Bout(subtrator_completo_bout[0]));
  Somador_Completo somador_completo (
    .A(A_B_2[2]), .B(A_B_2[1]), .Cin(A_B_2[0]), .Sum(somador_completo_sum[0]), .Cout(somador_completo_sum[1]));
  Multiplexer #(.width(2), .enable("false")) multiplexer_1 (
    .in0(subtrator_completo_bout), .in1(somador_completo_sum), .out(S_Cout), .sel(in_3));
endmodule

module Meio_Sub_Meio_Som_Demux (
  input  [1:0] A_B,
  input  in_2,
  output [1:0] S_Tout,
  output [1:0] Cout_S
);

  wire [1:0] demultiplexer_1_out0, demultiplexer_1_out1;

  Demultiplexer #(.width(2), .enable("false")) demultiplexer_1 (
    .out0(demultiplexer_1_out0), .out1(demultiplexer_1_out1), .in(A_B), .sel(in_2));
  Meio_Subtrator meio_subtrator (
    .A(demultiplexer_1_out0[0]), .B(demultiplexer_1_out0[1]), .S(S_Tout[1]), .Tout(S_Tout[0]));
  Meio_Somador meio_somador (
    .A(demultiplexer_1_out1[0]), .B(demultiplexer_1_out1[1]), .Sum(Cout_S[0]), .Cout(Cout_S[1]));
endmodule

module Somador_Subtrator_Demux (
  input  [2:0] A_B_C,
  input  in_2,
  output [1:0] S_Tout,
  output [1:0] Cout_S
);

  wire [2:0] demultiplexer_1_out0, demultiplexer_1_out1;

  Demultiplexer #(.width(3), .enable("false")) demultiplexer_1 (
    .out0(demultiplexer_1_out0), .out1(demultiplexer_1_out1), .in(A_B_C), .sel(in_2));
  Somador_Completo somador_completo (
    .A(demultiplexer_1_out1[2]), .B(demultiplexer_1_out1[1]), .Cin(demultiplexer_1_out1[0]), .Sum(Cout_S[0]),
    .Cout(Cout_S[1]));
  Subtrator_Completo subtrator_completo (
    .A(demultiplexer_1_out0[2]), .B(demultiplexer_1_out0[1]), .Bin(demultiplexer_1_out0[0]), .Sub(S_Tout[1]),
    .Bout(S_Tout[0]));
endmodule
