// Logisim project Relatorio2.circ as structural Verilog
module Meio_Somador (
  input  A,
  input  B,
  output Sum,
  output Cout
);

  xor xor_1 (Sum, A, B);
  and and_1 (Cout, A, B);
endmodule

module Somador_Completo (
  input  A,
  input  B,
  input  Cin,
  output Sum,
  output Cout
);

  wire meio_somador_1_cout, meio_somador_1_sum, meio_somador_2_cout;

  Meio_Somador meio_somador_1 (.A(A), .B(B), .Sum(meio_somador_1_sum), .Cout(meio_somador_1_cout));
  Meio_Somador meio_somador_2 (.A(meio_somador_1_sum), .B(Cin), .Sum(Sum), .Cout(meio_somador_2_cout));
  or or_1 (Cout, meio_somador_2_cout, meio_somador_1_cout);
endmodule

module Exercicio1 (
  input  [3:0] A,
  input  [3:0] B,
  input  Cin,
  output Cout,
  output [3:0] S
);

  wire multiplexer_1_out, multiplexer_2_out, multiplexer_3_out, multiplexer_4_out, not_1_out, not_2_out,
       not_3_out, not_4_out, somador_completo_2_cout, somador_completo_3_cout, somador_completo_4_cout;

  Hex_Digit_Display hex_digit_display_1 (.value(S));  // open: dp
  not not_1 (not_1_out, B[3]);
  Multiplexer #(.enable("false")) multiplexer_1 (.in0(B[3]), .in1(not_1_out), .out(multiplexer_1_out), .sel(Cin));
  Somador_Completo somador_completo_1 (
    .A(A[3]), .B(multiplexer_1_out), .Cin(somador_completo_2_cout), .Sum(S[3]), .Cout(Cout));
  not not_2 (not_2_out, B[2]);
  Multiplexer #(.enable("false")) multiplexer_2 (.in0(B[2]), .in1(not_2_out), .out(multiplexer_2_out), .sel(Cin));
  Somador_Completo somador_completo_2 (
    .A(A[2]), .B(multiplexer_2_out), .Cin(somador_completo_3_cout), .Sum(S[2]), .Cout(somador_completo_2_cout));
  not not_3 (not_3_out, B[1]);
  Multiplexer #(.enable("false")) multiplexer_3 (.in0(B[1]), .in1(not_3_out), .out(multiplexer_3_out), .sel(Cin));
  Somador_Completo somador_completo_3 (
    .A(A[1]), .B(multiplexer_3_out), .Cin(somador_completo_4_cout), .Sum(S[1]), .Cout(somador_completo_3_cout));
  not not_4 (not_4_out, B[0]);
  Multiplexer #(.enable("false")) multiplexer_4 (.in0(B[0]), .in1(not_4_out), .out(multiplexer_4_out), .sel(Cin));
  Somador_Completo somador_completo_4 (
    .A(A[0]), .B(multiplexer_4_out), .Cin(Cin), .Sum(S[0]), .Cout(somador_completo_4_cout));
endmodule

module \Multiplicação  (
  input  A0,
  input  A1,
  input  B1,
  input  B0,
  output P3,
  output P2,
  output P1,
  output P0
);

  wire and_1_out, and_2_out, and_3_out, meio_somador_2_cout;

  and and_1 (and_1_out, A0, B1);
  and and_2 (and_2_out, A0, B0);
  Meio_Somador meio_somador_1 (.A(meio_somador_2_cout), .B(and_1_out), .Sum(P2), .Cout(P3));
  and and_3 (and_3_out, A1, B1);
  Meio_Somador meio_somador_2 (.A(and_3_out), .B(and_2_out), .Sum(P1), .Cout(meio_somador_2_cout));
  and and_4 (P0, A1, B0);
endmodule

module Registrador_Deslocamento (
  input  [3:0] D,
  input  Clock,
  input  Carga,
  input  Clear,
  output [3:0] Q
);

  wire multiplexer_1_out, multiplexer_2_out, multiplexer_3_out, multiplexer_4_out;

  Multiplexer #(.enable("false")) multiplexer_1 (.in0(Q[0]), .in1(D[0]), .out(multiplexer_1_out), .sel(Carga));
  D_Flip_Flop d_ff_1 (.clk(Clock), .D(multiplexer_1_out), .Q(Q[0]), .reset(Clear));  // open: Qn, preset, en
  Multiplexer #(.enable("false")) multiplexer_2 (.in0(Q[1]), .in1(D[1]), .out(multiplexer_2_out), .sel(Carga));
  D_Flip_Flop d_ff_2 (.clk(Clock), .D(multiplexer_2_out), .Q(Q[1]), .reset(Clear));  // open: Qn, preset, en
  Multiplexer #(.enable("false")) multiplexer_3 (.in0(Q[2]), .in1(D[2]), .out(multiplexer_3_out), .sel(Carga));
  D_Flip_Flop d_ff_3 (.clk(Clock), .D(multiplexer_3_out), .Q(Q[2]), .reset(Clear));  // open: Qn, preset, en
  D_Flip_Flop d_ff_4 (.clk(Clock), .D(multiplexer_4_out), .Q(Q[3]), .reset(Clear));  // open: Qn, preset, en
  Multiplexer #(.enable("false")) multiplexer_4 (.in0(Q[3]), .in1(D[3]), .out(multiplexer_4_out), .sel(Carga));
endmodule
